// Digital circuit DPM_Board.dig as structural Verilog
module DPM_Board (
  input  in_2,
  input  in_3,
  input  in_4,
  input  clk,
  input  in_6,
  input  in_7,
  input  in_8,
  input  in_9,
  input  in_10,
  input  in_11,
  input  in_12,
  input  in_13,
  input  in_14,
  input  in_15,
  input  in_16,
  input  in_17,
  output DPM
);

  wire _744040_1_q0, _744040_1_q1, _744040_1_q2, _744040_1_q3, _744040_1_q4, _744040_1_q5, _744040_1_q6,
       _744040_1_q7, _744040_1_q8, _744040_1_q9, _744040_1_q10, _744040_1_q11, wrapper12bit_1_cnt_a0,
       wrapper12bit_1_cnt_a1, wrapper12bit_1_cnt_a2, wrapper12bit_1_cnt_a3, wrapper12bit_1_cnt_a4,
       wrapper12bit_1_cnt_a5, wrapper12bit_1_cnt_a6, wrapper12bit_1_cnt_a7, wrapper12bit_1_cnt_a8,
       wrapper12bit_1_cnt_a9, wrapper12bit_1_cnt_a10, wrapper12bit_1_cnt_a11;

  _744040 _744040_1 (
    .nCP(clk), .MR(in_2), .Q0(_744040_1_q0), .Q1(_744040_1_q1), .Q2(_744040_1_q2), .Q3(_744040_1_q3),
    .Q4(_744040_1_q4), .Q5(_744040_1_q5), .Q6(_744040_1_q6), .Q7(_744040_1_q7), .Q8(_744040_1_q8),
    .Q9(_744040_1_q9), .Q10(_744040_1_q10), .Q11(_744040_1_q11));
  Wrapper12bit wrapper12bit_1 (
    .M0(in_3), .M1(in_4), .A0(_744040_1_q0), .A1(_744040_1_q1), .A2(_744040_1_q2), .A3(_744040_1_q3),
    .A4(_744040_1_q4), .A5(_744040_1_q5), .A6(_744040_1_q6), .A7(_744040_1_q7), .A8(_744040_1_q8),
    .A9(_744040_1_q9), .A10(_744040_1_q10), .A11(_744040_1_q11), .CNT_A0(wrapper12bit_1_cnt_a0),
    .CNT_A1(wrapper12bit_1_cnt_a1), .CNT_A2(wrapper12bit_1_cnt_a2), .CNT_A3(wrapper12bit_1_cnt_a3),
    .CNT_A4(wrapper12bit_1_cnt_a4), .CNT_A5(wrapper12bit_1_cnt_a5), .CNT_A6(wrapper12bit_1_cnt_a6),
    .CNT_A7(wrapper12bit_1_cnt_a7), .CNT_A8(wrapper12bit_1_cnt_a8), .CNT_A9(wrapper12bit_1_cnt_a9),
    .CNT_A10(wrapper12bit_1_cnt_a10), .CNT_A11(wrapper12bit_1_cnt_a11));
  Cmp12bits cmp12bits_1 (
    .A0(wrapper12bit_1_cnt_a0), .A1(wrapper12bit_1_cnt_a1), .A2(wrapper12bit_1_cnt_a2),
    .A3(wrapper12bit_1_cnt_a3), .A4(wrapper12bit_1_cnt_a4), .A5(wrapper12bit_1_cnt_a5),
    .A6(wrapper12bit_1_cnt_a6), .A7(wrapper12bit_1_cnt_a7), .A8(wrapper12bit_1_cnt_a8),
    .A9(wrapper12bit_1_cnt_a9), .A10(wrapper12bit_1_cnt_a10), .A11(wrapper12bit_1_cnt_a11), .B0(in_6),
    .B1(in_7), .B2(in_8), .B3(in_9), .B4(in_10), .B5(in_11), .B6(in_12), .B7(in_13), .B8(in_14), .B9(in_15),
    .B10(in_16), .B11(in_17), .Ia_gt_b(1'b0), .Ia_lt_b(1'b0), .Ia_eq_b(1'b1), .Oa_lt_b(DPM));  // open: Oa_gt_b, Oa_eq_b

  // Notes on the sheet:
  //   clk: Hz: 500
endmodule
